// Logisim project Lab 3.circ as structural Verilog
module Main (
);

  wire Clock, MemRead, Memwrite;
  wire [5:0] Funct, Opcode;
  wire [7:0] ALUResult;
  wire [15:6] Immediate;
  wire [25:16] Ins;
  wire [31:0] DataOut, PC, RData2, ToPC;

  Clock clock_1 (.out(Clock));
  Instruction_Memory instruction_memory_1 (.PC(PC), .Ins({Ins, Immediate, Funct}), .Opcode(Opcode));
  PC pc_1 (.ToPC(ToPC), .Clk(Clock), .PC(PC));
  Register_File register_file_1 ();  // open: WrAddr, WrData, WrReg, RdAddr1, RdAddr2, RdData1, RdData2, Clock
  ALU alu_1 ();  // open: ALUCtl, A, B, ALUResult, Zero, Overflow, Shamt
  RAM #(.dataWidth(32), .bus("separate")) ram_1 (
    .addr(ALUResult), .din(RData2), .data(DataOut), .str(Memwrite), .clk(Clock), .ld(MemRead));  // open: sel, clr
  // Probe on nothing
  // Probe on nothing
  // Probe on nothing
  // Probe on nothing
  // Probe on nothing
  // Probe on nothing
  // Probe on nothing
  // Probe on nothing
  // Probe on nothing
  // Probe on nothing

  // Other names for the same wires on the sheet: rt[4:0] = Ins[20:16]; rs[4:0] = Ins[25:21]; Immediate[5:0] = Funct;
  //   Ins[15:0] = {Immediate, Funct}; SignExt[31:0] = {{17{Immediate[15]}}, Immediate[14:6], Funct};
  //   Shamt[4:0] = Immediate[10:6]; rd[4:0] = Immediate[15:11]

  // Notes on the sheet:
  //   Sign Extender
endmodule

module ALU (
  input  [2:0] ALUCtl,
  input  [31:0] A,
  input  [31:0] B,
  input  [4:0] Shamt,
  output [31:0] ALUResult,
  output Zero,
  output Overflow
);

  wire comparator_1_lt, comparator_2_lt, comparator_3_eq, comparator_4_eq, or_2_out;
  wire [31:0] ADD, AND, NOR, OR, SLL, SLT, SLTU, SRL, SUB, XOR;

  assign XOR = A ^ B;  // XOR_Gate xor_1, 32 bits wide
  Adder #(.width(32)) adder_1 (.a(A), .b(B), .out(ADD));  // open: cin, cout
  Subtractor #(.width(32)) subtractor_1 (.a(A), .b(B), .out(SUB));  // open: bin, bout
  assign AND = A & B;  // AND_Gate and_1, 32 bits wide
  assign OR = A | B;  // OR_Gate or_1, 32 bits wide
  assign NOR = ~(A | B);  // NOR_Gate nor_1, 32 bits wide
  Comparator #(.width(32)) comparator_1 (.a(A), .b(B), .lt(comparator_1_lt));  // open: gt, eq
  assign SLT = {{31{1'b0}}, comparator_1_lt};  // Bit_Extender bit_extender_1
  Shifter #(.width(32)) shifter_1 (.in(B), .\dist (Shamt), .out(SLL));
  Shifter #(.width(32), .shift("lr")) shifter_2 (.in(B), .\dist (Shamt), .out(SRL));
  Comparator #(.width(32), .mode("unsigned")) comparator_2 (.a(A), .b(B), .lt(comparator_2_lt));  // open: gt, eq
  assign SLTU = {{31{1'b0}}, comparator_2_lt};  // Bit_Extender bit_extender_2
  Multiplexer #(.select(3), .width(32), .enable("false")) multiplexer_1 (
    .in0(AND), .in1(ADD), .in2(OR), .in3(SUB), .in4(SLT), .in5(XOR), .in6(SRL), .in7(SLL), .out(ALUResult),
    .sel(ALUCtl));
  Comparator #(.width(3)) comparator_3 (.a(3'b001), .b(ALUCtl), .eq(comparator_3_eq));  // open: gt, lt
  Comparator #(.width(3)) comparator_4 (.a(ALUCtl), .b(3'b011), .eq(comparator_4_eq));  // open: gt, lt
  Overflow_Unit overflow_unit_1 (
    .Add(comparator_3_eq), .Sub(comparator_4_eq), .ASign(A[31]), .BSign(B[31]), .ResultSign(ALUResult[31]),
    .Overflow(Overflow));
  or or_2 (or_2_out, ALUResult[0], ALUResult[1], ALUResult[2], ALUResult[3], ALUResult[4], ALUResult[5], ALUResult[6], ALUResult[7], ALUResult[8], ALUResult[9], ALUResult[10], ALUResult[11], ALUResult[12], ALUResult[13], ALUResult[14], ALUResult[15], ALUResult[16], ALUResult[17], ALUResult[18], ALUResult[19], ALUResult[20], ALUResult[21], ALUResult[22], ALUResult[23], ALUResult[24], ALUResult[25], ALUResult[26], ALUResult[27], ALUResult[28], ALUResult[29], ALUResult[30], ALUResult[31]);
  not not_1 (Zero, or_2_out);

  // Other names for the same wires on the sheet: ASign = A[31]; ResultSign = ALUResult[31]; BSign = B[31]

  // Notes on the sheet:
  //   ALUCtl for ADD on top port
  //   ALUCtl for SUB on second port
endmodule

module Register_File (
  input  [4:0] WrAddr,
  input  [31:0] WrData,
  input  WrReg,
  input  [4:0] RdAddr1,
  input  [4:0] RdAddr2,
  input  Clock,
  output [31:0] RdData1,
  output [31:0] RdData2
);

  wire and_1_out, and_2_out, comparator_1_eq, comparator_2_eq, comparator_3_eq, comparator_4_eq, not_1_out,
       not_2_out, WrReg0, WrReg1, WrReg2, WrReg3, WrReg4, WrReg5, WrReg6, WrReg7, WrReg8, WrReg9, WrReg10,
       WrReg11, WrReg12, WrReg13, WrReg14, WrReg15, WrReg16, WrReg17, WrReg18, WrReg19, WrReg20, WrReg21,
       WrReg22, WrReg23, WrReg24, WrReg25, WrReg26, WrReg27, WrReg28, WrReg29, WrReg30, WrReg31;
  wire [31:0] multiplexer_1_out, multiplexer_2_out, RegData1, RegData2, RegData3, RegData4, RegData5,
       RegData6, RegData7, RegData8, RegData9, RegData10, RegData11, RegData12, RegData13, RegData14,
       RegData15, RegData16, RegData17, RegData18, RegData19, RegData20, RegData21, RegData22, RegData23,
       RegData24, RegData25, RegData26, RegData27, RegData28, RegData29, RegData30, RegData31;

  Demultiplexer #(.select(5), .enable("false")) demultiplexer_1 (
    .out0(WrReg0), .out1(WrReg1), .out2(WrReg2), .out3(WrReg3), .out4(WrReg4), .out5(WrReg5), .out6(WrReg6),
    .out7(WrReg7), .out8(WrReg8), .out9(WrReg9), .out10(WrReg10), .out11(WrReg11), .out12(WrReg12),
    .out13(WrReg13), .out14(WrReg14), .out15(WrReg15), .out16(WrReg16), .out17(WrReg17), .out18(WrReg18),
    .out19(WrReg19), .out20(WrReg20), .out21(WrReg21), .out22(WrReg22), .out23(WrReg23), .out24(WrReg24),
    .out25(WrReg25), .out26(WrReg26), .out27(WrReg27), .out28(WrReg28), .out29(WrReg29), .out30(WrReg30),
    .out31(WrReg31), .in(WrReg), .sel(WrAddr));
  // Probe on RegData4
  Register #(.width(32)) Reg4 (.D(WrData), .en(WrReg4), .Q(RegData4), .clk(Clock));  // open: clr
  // Probe on RegData8
  Register #(.width(32)) Reg8 (.D(WrData), .en(WrReg8), .Q(RegData8), .clk(Clock));  // open: clr
  // Probe on RegData12
  Register #(.width(32)) Reg12 (.D(WrData), .en(WrReg12), .Q(RegData12), .clk(Clock));  // open: clr
  // Probe on RegData16
  Register #(.width(32)) Reg16 (.D(WrData), .en(WrReg16), .Q(RegData16), .clk(Clock));  // open: clr
  // Probe on RegData20
  Register #(.width(32)) Reg20 (.D(WrData), .en(WrReg20), .Q(RegData20), .clk(Clock));  // open: clr
  // Probe on RegData24
  Register #(.width(32)) Reg24 (.D(WrData), .en(WrReg24), .Q(RegData24), .clk(Clock));  // open: clr
  // Probe on RegData28
  Register #(.width(32)) Reg28 (.D(WrData), .en(WrReg28), .Q(RegData28), .clk(Clock));  // open: clr
  Register #(.width(32)) Reg1 (.D(WrData), .en(WrReg1), .Q(RegData1), .clk(Clock));  // open: clr
  Register #(.width(32)) Reg5 (.D(WrData), .en(WrReg5), .Q(RegData5), .clk(Clock));  // open: clr
  Register #(.width(32)) Reg9 (.D(WrData), .en(WrReg9), .Q(RegData9), .clk(Clock));  // open: clr
  Register #(.width(32)) Reg13 (.D(WrData), .en(WrReg13), .Q(RegData13), .clk(Clock));  // open: clr
  Register #(.width(32)) Reg17 (.D(WrData), .en(WrReg17), .Q(RegData17), .clk(Clock));  // open: clr
  Register #(.width(32)) Reg21 (.D(WrData), .en(WrReg21), .Q(RegData21), .clk(Clock));  // open: clr
  Register #(.width(32)) Reg25 (.D(WrData), .en(WrReg25), .Q(RegData25), .clk(Clock));  // open: clr
  Register #(.width(32)) Reg29 (.D(WrData), .en(WrReg29), .Q(RegData29), .clk(Clock));  // open: clr
  // Probe on RegData1
  // Probe on RegData5
  // Probe on RegData9
  // Probe on RegData13
  // Probe on RegData17
  // Probe on RegData21
  // Probe on RegData25
  // Probe on RegData29
  // Probe on RegData2
  Register #(.width(32)) Reg2 (.D(WrData), .en(WrReg2), .Q(RegData2), .clk(Clock));  // open: clr
  // Probe on RegData6
  Register #(.width(32)) Reg6 (.D(WrData), .en(WrReg6), .Q(RegData6), .clk(Clock));  // open: clr
  // Probe on RegData10
  Register #(.width(32)) Reg10 (.D(WrData), .en(WrReg10), .Q(RegData10), .clk(Clock));  // open: clr
  // Probe on RegData14
  Register #(.width(32)) Reg14 (.D(WrData), .en(WrReg14), .Q(RegData14), .clk(Clock));  // open: clr
  // Probe on RegData18
  Register #(.width(32)) Reg18 (.D(WrData), .en(WrReg18), .Q(RegData18), .clk(Clock));  // open: clr
  // Probe on RegData22
  Register #(.width(32)) Reg22 (.D(WrData), .en(WrReg22), .Q(RegData22), .clk(Clock));  // open: clr
  // Probe on RegData26
  Register #(.width(32)) Reg26 (.D(WrData), .en(WrReg26), .Q(RegData26), .clk(Clock));  // open: clr
  // Probe on RegData30
  Register #(.width(32)) Reg30 (.D(WrData), .en(WrReg30), .Q(RegData30), .clk(Clock));  // open: clr
  // Probe on RegData3
  Register #(.width(32)) Reg3 (.D(WrData), .en(WrReg3), .Q(RegData3), .clk(Clock));  // open: clr
  // Probe on RegData7
  Register #(.width(32)) Reg7 (.D(WrData), .en(WrReg7), .Q(RegData7), .clk(Clock));  // open: clr
  // Probe on RegData11
  Register #(.width(32)) Reg11 (.D(WrData), .en(WrReg11), .Q(RegData11), .clk(Clock));  // open: clr
  // Probe on RegData15
  Register #(.width(32)) Reg15 (.D(WrData), .en(WrReg15), .Q(RegData15), .clk(Clock));  // open: clr
  // Probe on RegData19
  Register #(.width(32)) Reg19 (.D(WrData), .en(WrReg19), .Q(RegData19), .clk(Clock));  // open: clr
  // Probe on RegData23
  Register #(.width(32)) Reg23 (.D(WrData), .en(WrReg23), .Q(RegData23), .clk(Clock));  // open: clr
  // Probe on RegData27
  Register #(.width(32)) Reg27 (.D(WrData), .en(WrReg27), .Q(RegData27), .clk(Clock));  // open: clr
  // Probe on RegData31
  Register #(.width(32)) Reg31 (.D(WrData), .en(WrReg31), .Q(RegData31), .clk(Clock));  // open: clr
  Multiplexer #(.select(5), .width(32), .enable("false")) multiplexer_1 (
    .in0({32{1'b0}}), .in1(RegData1), .in2(RegData2), .in3(RegData3), .in4(RegData4), .in5(RegData5),
    .in6(RegData6), .in7(RegData7), .in8(RegData8), .in9(RegData9), .in10(RegData10), .in11(RegData11),
    .in12(RegData12), .in13(RegData13), .in14(RegData14), .in15(RegData15), .in16(RegData16),
    .in17(RegData17), .in18(RegData18), .in19(RegData19), .in20(RegData20), .in21(RegData21),
    .in22(RegData22), .in23(RegData23), .in24(RegData24), .in25(RegData25), .in26(RegData26),
    .in27(RegData27), .in28(RegData28), .in29(RegData29), .in30(RegData30), .in31(RegData31),
    .out(multiplexer_1_out), .sel(RdAddr1));
  Multiplexer #(.select(5), .width(32), .enable("false")) multiplexer_2 (
    .in0({32{1'b0}}), .in1(RegData1), .in2(RegData2), .in3(RegData3), .in4(RegData4), .in5(RegData5),
    .in6(RegData6), .in7(RegData7), .in8(RegData8), .in9(RegData9), .in10(RegData10), .in11(RegData11),
    .in12(RegData12), .in13(RegData13), .in14(RegData14), .in15(RegData15), .in16(RegData16),
    .in17(RegData17), .in18(RegData18), .in19(RegData19), .in20(RegData20), .in21(RegData21),
    .in22(RegData22), .in23(RegData23), .in24(RegData24), .in25(RegData25), .in26(RegData26),
    .in27(RegData27), .in28(RegData28), .in29(RegData29), .in30(RegData30), .in31(RegData31),
    .out(multiplexer_2_out), .sel(RdAddr2));
  Multiplexer #(.width(32), .enable("false")) multiplexer_3 (
    .in0(multiplexer_1_out), .in1(WrData), .out(RdData1), .sel(and_1_out));
  Comparator #(.width(5), .mode("unsigned")) comparator_1 (
    .a(WrAddr), .b(RdAddr2), .eq(comparator_1_eq));  // open: gt, lt
  Multiplexer #(.width(32), .enable("false")) multiplexer_4 (
    .in0(multiplexer_2_out), .in1(WrData), .out(RdData2), .sel(and_2_out));
  Comparator #(.width(5), .mode("unsigned")) comparator_2 (
    .a(WrAddr), .b(RdAddr1), .eq(comparator_2_eq));  // open: gt, lt
  and and_1 (and_1_out, comparator_2_eq, WrReg, not_1_out);
  and and_2 (and_2_out, comparator_1_eq, WrReg, not_2_out);
  Comparator #(.width(5), .mode("unsigned")) comparator_3 (
    .a(WrAddr), .b({5{1'b0}}), .eq(comparator_3_eq));  // open: gt, lt
  not not_1 (not_1_out, comparator_3_eq);
  Comparator #(.width(5), .mode("unsigned")) comparator_4 (
    .a(WrAddr), .b({5{1'b0}}), .eq(comparator_4_eq));  // open: gt, lt
  not not_2 (not_2_out, comparator_4_eq);
endmodule

module Overflow_Unit (
  input  Add,
  input  Sub,
  input  ASign,
  input  BSign,
  input  ResultSign,
  output Overflow
);

  wire and_1_out, and_2_out, or_1_out, xnor_1_out, xor_1_out, xor_2_out;

  xnor xnor_1 (xnor_1_out, ASign, BSign);
  xor xor_1 (xor_1_out, ASign, BSign);
  and and_1 (and_1_out, xnor_1_out, Add);
  and and_2 (and_2_out, xor_1_out, Sub);
  or or_1 (or_1_out, and_1_out, and_2_out);
  xor xor_2 (xor_2_out, ResultSign, ASign);
  and and_3 (Overflow, or_1_out, xor_2_out);

  // Notes on the sheet:
  //   Overflow occurs when doing addition and sign(A) == sign(B) && sign(result) != sign(A)
  //   Or
  //   Overflow occurs when doing subtraction and sign(A) != sign(B) && sign(result) != sign(A)
endmodule

module PC (
  input  [31:0] ToPC,
  input  Clk,
  output [31:0] PC
);

  Register #(.width(32)) register_1 (.D(ToPC), .Q(PC), .clk(Clk));  // open: en, clr
endmodule

module Instruction_Memory (
  input  [31:0] PC,
  output [25:0] Ins,
  output [5:0] Opcode
);

  wire [31:0] shifter_1_out;

  Shifter #(.width(32), .shift("lr")) shifter_1 (.in(PC), .\dist (5'b00010), .out(shifter_1_out));
  ROM #(.dataWidth(32)) rom_1 (.addr(shifter_1_out[7:0]), .data({Opcode, Ins}));  // open: sel
endmodule

module Control (
  input  Op31,
  input  Op30,
  input  Op29,
  input  Op28,
  input  Op27,
  input  Op26,
  output RegDst,
  output Jump,
  output Branch,
  output MemRead,
  output MemToReg,
  output ALUOp0,
  output ALUOp1,
  output ALUOp2,
  output MemWrite,
  output ALUSrc,
  output RegWrite,
  output JAL
);

  wire and_8_out, and_9_out, and_10_out, and_11_out, and_12_out, and_13_out, and_14_out, and_15_out,
       and_16_out, not_1_out, not_2_out, not_3_out, not_4_out, not_5_out, not_6_out, not_7_out, not_8_out,
       not_9_out, not_10_out, not_11_out, not_12_out, not_13_out, not_14_out, not_15_out, not_16_out,
       not_17_out, not_18_out, not_19_out, not_20_out, not_21_out, not_22_out, not_23_out;

  not not_1 (not_1_out, Op29);
  not not_2 (not_2_out, Op27);
  not not_3 (not_3_out, Op31);
  not not_4 (not_4_out, Op29);
  not not_5 (not_5_out, Op29);
  not not_6 (not_6_out, Op29);
  not not_7 (not_7_out, Op31);
  not not_8 (not_8_out, Op27);
  not not_9 (not_9_out, Op30);
  not not_10 (not_10_out, Op29);
  not not_11 (not_11_out, Op30);
  not not_12 (not_12_out, Op28);
  not not_13 (not_13_out, Op30);
  not not_14 (not_14_out, Op28);
  not not_15 (not_15_out, Op28);
  not not_16 (not_16_out, Op27);
  not not_17 (not_17_out, Op27);
  and and_1 (ALUOp2, Op29, Op28);
  and and_2 (MemWrite, Op29, Op27);
  or or_1 (ALUSrc, Op29, Op31);
  not not_18 (not_18_out, Op28);
  not not_19 (not_19_out, Op27);
  not not_20 (not_20_out, Op29);
  not not_21 (not_21_out, Op27);
  not not_22 (not_22_out, Op31);
  not not_23 (not_23_out, Op29);
  and and_3 (RegDst, not_1_out, not_2_out);
  and and_4 (Jump, not_3_out, Op27);
  and and_5 (Branch, not_4_out, Op28);
  and and_6 (MemRead, Op31, not_5_out);
  and and_7 (MemToReg, Op31, not_6_out);
  and and_8 (and_8_out, not_7_out, not_8_out, Op26);
  and and_9 (and_9_out, not_9_out, not_10_out, Op28);
  and and_10 (and_10_out, not_11_out, Op29, not_12_out);
  and and_11 (and_11_out, Op31, not_13_out, not_14_out);
  and and_12 (and_12_out, not_15_out, not_16_out);
  and and_13 (and_13_out, Op30, not_17_out);
  and and_14 (and_14_out, not_18_out, not_19_out);
  and and_15 (and_15_out, not_20_out, Op26);
  and and_16 (and_16_out, Op29, not_21_out);
  and and_17 (JAL, not_22_out, not_23_out, Op26);
  or or_2 (ALUOp0, and_8_out, and_9_out, and_10_out, and_11_out);
  or or_3 (ALUOp1, and_12_out, and_13_out, Op31);
  or or_4 (RegWrite, and_14_out, and_15_out, and_16_out);

  // Notes on the sheet:
  //   Same as Lab 2 (For the first part)
endmodule

module ALU_Control (
  input  ALUOp2,
  input  ALUOp1,
  input  ALUOp0,
  input  Func5,
  input  Func4,
  input  Func3,
  input  Func2,
  input  Func1,
  input  Func0,
  output ALUControl2,
  output ALUControl1,
  output ALUControl0,
  output JumpReg
);

  wire and_1_out, and_2_out, and_3_out, and_4_out, and_5_out, and_6_out, and_7_out, and_8_out, and_9_out,
       and_10_out, not_1_out, not_2_out, not_3_out, not_4_out, not_5_out, not_6_out, not_7_out, not_8_out,
       not_9_out, not_10_out, not_11_out, not_12_out, not_13_out, not_14_out, not_15_out, not_16_out,
       not_17_out, not_18_out, not_19_out, not_20_out, not_21_out, not_22_out, not_23_out, not_24_out,
       not_25_out, not_26_out, not_27_out, not_28_out, not_29_out, not_30_out;

  not not_1 (not_1_out, ALUOp2);
  not not_2 (not_2_out, ALUOp0);
  not not_3 (not_3_out, Func5);
  not not_4 (not_4_out, ALUOp2);
  not not_5 (not_5_out, ALUOp0);
  not not_6 (not_6_out, ALUOp2);
  not not_7 (not_7_out, ALUOp0);
  not not_8 (not_8_out, ALUOp2);
  not not_9 (not_9_out, ALUOp0);
  not not_10 (not_10_out, Func5);
  not not_11 (not_11_out, ALUOp2);
  not not_12 (not_12_out, ALUOp0);
  not not_13 (not_13_out, ALUOp2);
  not not_14 (not_14_out, ALUOp0);
  not not_15 (not_15_out, Func3);
  not not_16 (not_16_out, Func2);
  not not_17 (not_17_out, ALUOp1);
  not not_18 (not_18_out, ALUOp2);
  not not_19 (not_19_out, Func2);
  not not_20 (not_20_out, Func1);
  not not_21 (not_21_out, ALUOp2);
  not not_22 (not_22_out, Func3);
  not not_23 (not_23_out, ALUOp2);
  not not_24 (not_24_out, ALUOp2);
  not not_25 (not_25_out, ALUOp0);
  not not_26 (not_26_out, Func5);
  not not_27 (not_27_out, Func4);
  not not_28 (not_28_out, Func2);
  not not_29 (not_29_out, Func1);
  not not_30 (not_30_out, Func0);
  and and_1 (and_1_out, not_1_out, not_2_out, not_3_out);
  and and_2 (and_2_out, not_4_out, not_5_out, Func2, Func1);
  and and_3 (and_3_out, not_6_out, not_7_out, Func3);
  and and_4 (and_4_out, not_8_out, not_9_out, not_10_out);
  and and_5 (and_5_out, not_11_out, not_12_out, Func0);
  and and_6 (and_6_out, not_13_out, not_14_out, not_15_out, not_16_out, Func1);
  and and_7 (and_7_out, not_17_out, ALUOp0);
  and and_8 (and_8_out, not_18_out, not_19_out, not_20_out);
  and and_9 (and_9_out, not_21_out, Func5, not_22_out, Func1);
  and and_10 (and_10_out, not_23_out, ALUOp0);
  and and_11 (JumpReg, not_24_out, ALUOp1, not_25_out, not_26_out, not_27_out, Func3, not_28_out, not_29_out, not_30_out);
  or or_1 (ALUControl2, and_1_out, and_2_out, and_3_out);
  or or_2 (ALUControl1, and_4_out, and_5_out, and_6_out, and_7_out);
  or or_3 (ALUControl0, and_8_out, and_9_out, and_10_out);

  // Notes on the sheet:
  //   Same as lab 2, except add functionality for SLL and SRL
endmodule
